# Fritzing sketch circuit_design (saved by Fritzing 0.9.3b)

parts:
  U2 = DC-DC 2-24V Step Up Booster [part_number="XL6009 2a Boost Converter DC 6v" package=THT]
  NEOPIXEL1 = Neopixel Strip -- Black (30/m) [part_number=1376]
  Part1 = Arduino Nano (Rev3.0)
  R2 = Resistor [tolerance=±5% resistance=220 package=THT]
  R3 = Resistor [tolerance=±5% resistance=10k package=THT]
  S2 = Pushbutton [package="[THT]"]
  S3 = Pushbutton [package="[THT]"]
  R4 = Resistor [tolerance=±5% resistance=10k package=THT]
  U1_-_Main_Power_Switch1 = SWITCH-SPST-2 [package=switch-spst-vertical]
  Part2 = Adafruit Micro USB Breakout [part_number="Adafruit #1833"]

nets:
  N1: U2.pin1, U1_-_Main_Power_Switch1.O
  GND: U2.pin2, NEOPIXEL1.GND, Part1.GND, R3.Pin_1, R4.Pin_1
  N2: U2.pin3, Part2.VBUS
  N3: U2.pin4, Part2.GND
  N4: NEOPIXEL1.Din, R2.Pin_0
  5V: NEOPIXEL1.+5V, Part1.VIN, S2.Pin_1, S2.Pin_2, S3.Pin_2, U1_-_Main_Power_Switch1.P
  N5: Part1.D5, R3.Pin_0, S2.Pin_3, S2.Pin_4
  N6: Part1.D6, S3.Pin_3, S3.Pin_4, R4.Pin_0
  N7: Part1.D7, R2.Pin_1

custom parts:
  DC-DC 2-24V Step Up Booster: Convertisseur DC-DC 2-24V 2A
  Neopixel Strip -- Black (30/m): These NeoPixel strips have 30 digitally-addressable pixel LEDs per meter and are very affordable and are only 12.5 mm wide, 10 mm if you remove the strip from the casing.
  Adafruit Micro USB Breakout: Simple but effective - this breakout board has a USB Micro-B connector, with all 5 pins broken out. Great for pairing with a microcontroller with USB support, or adding USB 5V power to a project. We use a micro-AB connector with through-hole shielding pads for an excellent strong connection - it won't rip off by accident! Comes with one fully assembled and tested micro B breakout PCB and a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
